# Fritzing sketch schematic (saved by Fritzing 0.9.10b)
breadboards: 1

parts:
  MH-ET_LIVE_ESP32_DEVKIT1 = MH-ET LIVE ESP32 DEVKIT 38 pins
  MOTOR9 = Vibration Motor
  MOTOR13 = Vibration Motor
  MOTOR16 = Vibration Motor
  IC4 = ULN2803A [package=THT]
  Part1 = Lithium Ion Polymer Battery 3.7v 1200mAh [part_number=258]  # not connected
  M2 = MT3608 Module
  TP1 = TP4056 [chip_label=TP4056 package="DIP (Dual Inline) [THT]"]
  SparkFun_LiPo_Fuel_Gauge1 = SparkFun LiPo Fuel Gauge [part_number=TOL-10617]

nets:
  N1: MH-ET_LIVE_ESP32_DEVKIT1.IO32, IC4.In_3
  N2: MH-ET_LIVE_ESP32_DEVKIT1.IO33, IC4.In_2
  N3: MH-ET_LIVE_ESP32_DEVKIT1.IO25, IC4.In_1
  N4: MH-ET_LIVE_ESP32_DEVKIT1.GND, IC4.0V
  N5: MH-ET_LIVE_ESP32_DEVKIT1.5V, MOTOR9.POS, MOTOR13.POS, MOTOR16.POS, IC4.COM_-_Common
  N6: MH-ET_LIVE_ESP32_DEVKIT1.IO22, SparkFun_LiPo_Fuel_Gauge1.SCL
  N7: MH-ET_LIVE_ESP32_DEVKIT1.IO21, SparkFun_LiPo_Fuel_Gauge1.SDA
  N8: MOTOR9.NEG, IC4.Out_2
  N9: MOTOR13.NEG, IC4.Out_1
  N10: MOTOR16.NEG, IC4.Out_3
  N11: M2.pin1, TP1.pin6
  N12: M2.pin2, TP1.pin3
  N13: TP1.pin4, SparkFun_LiPo_Fuel_Gauge1.VCC
  N14: TP1.pin5, SparkFun_LiPo_Fuel_Gauge1.GND

notes:
  0
  1
  2
  Option B: LiPo battery
  Option A: USB power bank

custom parts:
  MH-ET LIVE ESP32 DEVKIT 38 pins: http://mh.nodebb.com/topic/2/mh-et-live-esp32-devkit
  Vibration Motor: An eccentric vibration motor!
  Lithium Ion Polymer Battery 3.7v 1200mAh: Lithium ion polymer (also known as 'lipo' or 'lipoly') batteries are thin, light and powerful. The output ranges from 4.2V when completely charged to 3.7V. This battery has a capacity of 1200mAh for a total of about 4.5 Wh. The batteries come pre-attached with a genuine 2-pin JST-PH connector as shown and include the necessary protection circuitry.
  MT3608 Module: MT3608 Boost Converter Module Links: Aerosemi MT3608 2A Step Up Converter datasheet
  TP4056: A DIP stand-in part for whatever IC you want. With 6 pins on a 300mil dual inline package (DIP) footprint.
  SparkFun LiPo Fuel Gauge: LiPo batteries are a great way to power your projects. They’re small, lightweight, and pack a pretty good punch for their size. Unfortunately, even the best batteries eventually run low on power and when they do it’s often unexpected (and at the worst time). Don’t be caught by surprise next time your board suddenly powers-down! The SparkFun LiPo Fuel Gauge connects your battery to your project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
