# Fritzing sketch schematic (saved by Fritzing 0.9.10b)
breadboards: 1

parts:
  MOTOR9 = Vibration Motor
  MOTOR10 = Vibration Motor
  MOTOR13 = Vibration Motor
  MOTOR14 = Vibration Motor
  MOTOR15 = Vibration Motor
  MOTOR16 = Vibration Motor
  Part1 = Lithium Ion Polymer Battery 3.7v 1200mAh [part_number=258]  # not connected
  M2 = MT3608 Module
  TP1 = TP4056 [chip_label=TP4056 package="DIP (Dual Inline) [THT]"]
  SparkFun_LiPo_Fuel_Gauge1 = SparkFun LiPo Fuel Gauge [part_number=TOL-10617]
  MH-ET_LIVE_ESP32_DEVKIT2 = MH-ET LIVE ESP32 DEVKIT 38 pins
  IC5 = ULN2803A [package=THT]

nets:
  N1: MOTOR9.POS, MOTOR10.POS, MOTOR13.POS, MOTOR14.POS, MOTOR15.POS, MOTOR16.POS, M2.pin3, MH-ET_LIVE_ESP32_DEVKIT2.5V, IC5.COM_-_Common
  N2: MOTOR9.NEG, IC5.Out_2
  N3: MOTOR10.NEG, IC5.Out_5
  N4: MOTOR13.NEG, IC5.Out_1
  N5: MOTOR14.NEG, IC5.Out_4
  N6: MOTOR15.NEG, IC5.Out_6
  N7: MOTOR16.NEG, IC5.Out_3
  N8: M2.pin1, TP1.pin6
  N9: M2.pin2, TP1.pin3
  N10: M2.pin4, MH-ET_LIVE_ESP32_DEVKIT2.GND#58, IC5.0V
  N11: TP1.pin4, SparkFun_LiPo_Fuel_Gauge1.VCC
  N12: TP1.pin5, SparkFun_LiPo_Fuel_Gauge1.GND
  N13: MH-ET_LIVE_ESP32_DEVKIT2.IO32, IC5.In_6
  N14: MH-ET_LIVE_ESP32_DEVKIT2.IO33, IC5.In_5
  N15: MH-ET_LIVE_ESP32_DEVKIT2.IO25, IC5.In_4
  N16: MH-ET_LIVE_ESP32_DEVKIT2.IO26, IC5.In_3
  N17: MH-ET_LIVE_ESP32_DEVKIT2.IO27, IC5.In_2
  N18: MH-ET_LIVE_ESP32_DEVKIT2.IO14, IC5.In_1

notes:
  Thumb
  Index
  Middle
  Option B: LiPo battery
  Option A: USB power bank
  Ring
  Pinky
  Wrist

custom parts:
  Vibration Motor: An eccentric vibration motor!
  Lithium Ion Polymer Battery 3.7v 1200mAh: Lithium ion polymer (also known as 'lipo' or 'lipoly') batteries are thin, light and powerful. The output ranges from 4.2V when completely charged to 3.7V. This battery has a capacity of 1200mAh for a total of about 4.5 Wh. The batteries come pre-attached with a genuine 2-pin JST-PH connector as shown and include the necessary protection circuitry.
  MT3608 Module: MT3608 Boost Converter Module Links: Aerosemi MT3608 2A Step Up Converter datasheet
  TP4056: A DIP stand-in part for whatever IC you want. With 6 pins on a 300mil dual inline package (DIP) footprint.
  SparkFun LiPo Fuel Gauge: LiPo batteries are a great way to power your projects. They’re small, lightweight, and pack a pretty good punch for their size. Unfortunately, even the best batteries eventually run low on power and when they do it’s often unexpected (and at the worst time). Don’t be caught by surprise next time your board suddenly powers-down! The SparkFun LiPo Fuel Gauge connects your battery to your project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
  MH-ET LIVE ESP32 DEVKIT 38 pins: http://mh.nodebb.com/topic/2/mh-et-live-esp32-devkit
