# Fritzing sketch schematic (saved by Fritzing 1.0.1rc)
breadboards: 1

parts:
  MH-ET_LIVE_ESP32_DEVKIT1 = MH-ET LIVE ESP32 DEVKIT 38 pins
  MOTOR1 = Vibration Motor
  MOTOR2 = Vibration Motor
  MOTOR3 = Vibration Motor
  MOTOR4 = Vibration Motor
  MOTOR5 = Vibration Motor
  MOTOR6 = Vibration Motor
  MOTOR7 = Vibration Motor
  MOTOR8 = Vibration Motor
  MOTOR9 = Vibration Motor
  MOTOR10 = Vibration Motor
  MOTOR12 = Vibration Motor
  MOTOR13 = Vibration Motor
  MOTOR14 = Vibration Motor
  MOTOR15 = Vibration Motor
  MOTOR16 = Vibration Motor
  IC3 = ULN2803A [package=THT]
  IC4 = ULN2803A [package=THT]
  MOTOR11 = Vibration Motor
  Part1 = 16-Channel 12-bit PCA9685 PWM/Servo Driver
  TP2 = TP4056 [chip_label=TP4056 package="DIP (Dual Inline) [THT]"]
  Part2 = Lithium Ion Polymer Battery 3.7v 1200mAh [part_number=258]  # not connected
  M3 = MT3608 Module
  SparkFun_LiPo_Fuel_Gauge1 = SparkFun LiPo Fuel Gauge [part_number=TOL-10617]

nets:
  N1: MH-ET_LIVE_ESP32_DEVKIT1.3V3, MOTOR1.POS, MOTOR2.POS, MOTOR3.POS, MOTOR4.POS, MOTOR5.POS, MOTOR6.POS, MOTOR7.POS, MOTOR8.POS, MOTOR9.POS, MOTOR10.POS, MOTOR12.POS, MOTOR13.POS, MOTOR14.POS, MOTOR15.POS, MOTOR16.POS, IC3.COM_-_Common, IC4.COM_-_Common, MOTOR11.POS, Part1.V+, M3.pin3
  5V: MH-ET_LIVE_ESP32_DEVKIT1.5V, Part1.VCC
  N2: MH-ET_LIVE_ESP32_DEVKIT1.IO22, Part1.SCL, SparkFun_LiPo_Fuel_Gauge1.SCL
  N3: MH-ET_LIVE_ESP32_DEVKIT1.IO21, Part1.SDA, SparkFun_LiPo_Fuel_Gauge1.SDA
  GND: MH-ET_LIVE_ESP32_DEVKIT1.GND, IC3.0V, IC4.0V, Part1.GND, M3.pin4
  N4: MOTOR1.NEG, IC3.Out_1
  N5: MOTOR2.NEG, IC3.Out_2
  N6: MOTOR3.NEG, IC3.Out_3
  N7: MOTOR4.NEG, IC3.Out_4
  N8: MOTOR5.NEG, IC3.Out_5
  N9: MOTOR6.NEG, IC3.Out_6
  N10: MOTOR7.NEG, IC3.Out_7
  N11: MOTOR8.NEG, IC3.Out_8
  N12: MOTOR9.NEG, IC4.Out_4
  N13: MOTOR10.NEG, IC4.Out_7
  N14: MOTOR12.NEG, IC4.Out_2
  N15: MOTOR13.NEG, IC4.Out_3
  N16: MOTOR14.NEG, IC4.Out_6
  N17: MOTOR15.NEG, IC4.Out_8
  N18: MOTOR16.NEG, IC4.Out_5
  N19: IC3.In_1, Part1.8
  N20: IC3.In_2, Part1.9
  N21: IC3.In_3, Part1.10
  N22: IC3.In_4, Part1.11
  N23: IC3.In_5, Part1.12
  N24: IC3.In_6, Part1.13
  N25: IC3.In_7, Part1.14
  N26: IC3.In_8, Part1.15
  N27: IC4.In_1, Part1.0
  N28: IC4.In_2, Part1.1
  N29: IC4.In_3, Part1.2
  N30: IC4.In_4, Part1.3
  N31: IC4.In_5, Part1.4
  N32: IC4.In_6, Part1.5
  N33: IC4.In_7, Part1.6
  N34: IC4.In_8, Part1.7
  N35: IC4.Out_1, MOTOR11.NEG
  N36: TP2.pin3, M3.pin2
  N37: TP2.pin4, SparkFun_LiPo_Fuel_Gauge1.VCC
  N38: TP2.pin5, SparkFun_LiPo_Fuel_Gauge1.GND
  N39: TP2.pin6, M3.pin1

notes:
  Option B: LiPo battery
  Option A: USB power bank

custom parts:
  MH-ET LIVE ESP32 DEVKIT 38 pins: http://mh.nodebb.com/topic/2/mh-et-live-esp32-devkit
  Vibration Motor: An eccentric vibration motor!
  16-Channel 12-bit PCA9685 PWM/Servo Driver: The Adafruit 16-Channel 12-bit PWM/Servo Driver will drive up to 16 servos over I2C with only 2 pins. The on-board PCA9685 PWM controller will drive all 16 channels simultaneously with no additional processing overhead. What's more, you can chain up to 62 of them to control up to 992 servos - all with the same 2 pins
  TP4056: A DIP stand-in part for whatever IC you want. With 6 pins on a 300mil dual inline package (DIP) footprint.
  Lithium Ion Polymer Battery 3.7v 1200mAh: Lithium ion polymer (also known as 'lipo' or 'lipoly') batteries are thin, light and powerful. The output ranges from 4.2V when completely charged to 3.7V. This battery has a capacity of 1200mAh for a total of about 4.5 Wh. The batteries come pre-attached with a genuine 2-pin JST-PH connector as shown and include the necessary protection circuitry.
  MT3608 Module: MT3608 Boost Converter Module Links: Aerosemi MT3608 2A Step Up Converter datasheet
  SparkFun LiPo Fuel Gauge: LiPo batteries are a great way to power your projects. They’re small, lightweight, and pack a pretty good punch for their size. Unfortunately, even the best batteries eventually run low on power and when they do it’s often unexpected (and at the worst time). Don’t be caught by surprise next time your board suddenly powers-down! The SparkFun LiPo Fuel Gauge connects your battery to your project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
