# Fritzing sketch schematic (saved by Fritzing 1.0.1rc)
breadboards: 3

parts:
  MH-ET_LIVE_ESP32_DEVKIT1 = MH-ET LIVE ESP32 DEVKIT 38 pins
  MOTOR1 = Vibration Motor
  MOTOR2 = Vibration Motor
  MOTOR3 = Vibration Motor
  MOTOR4 = Vibration Motor
  MOTOR5 = Vibration Motor
  MOTOR6 = Vibration Motor
  MOTOR7 = Vibration Motor
  MOTOR8 = Vibration Motor
  MOTOR9 = Vibration Motor
  MOTOR10 = Vibration Motor
  MOTOR12 = Vibration Motor
  MOTOR13 = Vibration Motor
  MOTOR14 = Vibration Motor
  MOTOR15 = Vibration Motor
  MOTOR16 = Vibration Motor
  IC3 = ULN2803A [package=THT]
  IC4 = ULN2803A [package=THT]
  MOTOR11 = Vibration Motor
  Part1 = 16-Channel 12-bit PCA9685 PWM/Servo Driver
  TP2 = TP4056 [chip_label=TP4056 package="DIP (Dual Inline) [THT]"]
  Part2 = Lithium Ion Polymer Battery 3.7v 1200mAh [part_number=258]  # not connected
  M3 = MT3608 Module
  SparkFun_LiPo_Fuel_Gauge1 = SparkFun LiPo Fuel Gauge [part_number=TOL-10617]
  IC5 = ULN2803A [package=THT]
  IC6 = ULN2803A [package=THT]
  Part3 = 16-Channel 12-bit PCA9685 PWM/Servo Driver
  MOTOR17 = Vibration Motor
  MOTOR18 = Vibration Motor
  MOTOR19 = Vibration Motor
  MOTOR20 = Vibration Motor
  MOTOR21 = Vibration Motor
  MOTOR22 = Vibration Motor
  MOTOR23 = Vibration Motor
  MOTOR24 = Vibration Motor
  MOTOR25 = Vibration Motor
  MOTOR26 = Vibration Motor
  MOTOR27 = Vibration Motor
  MOTOR28 = Vibration Motor
  MOTOR29 = Vibration Motor
  MOTOR30 = Vibration Motor
  MOTOR31 = Vibration Motor
  IC7 = ULN2803A [package=THT]
  MOTOR32 = Vibration Motor
  MOTOR33 = Vibration Motor
  MOTOR34 = Vibration Motor
  MOTOR35 = Vibration Motor
  MOTOR36 = Vibration Motor
  MOTOR37 = Vibration Motor
  MOTOR38 = Vibration Motor
  MOTOR39 = Vibration Motor
  MOTOR40 = Vibration Motor

nets:
  VCC: MH-ET_LIVE_ESP32_DEVKIT1.3V3, Part1.VCC, Part3.VCC
  N1: MH-ET_LIVE_ESP32_DEVKIT1.IO32, IC7.In_8
  N2: MH-ET_LIVE_ESP32_DEVKIT1.IO33, IC7.In_7
  N3: MH-ET_LIVE_ESP32_DEVKIT1.IO25, IC7.In_6
  N4: MH-ET_LIVE_ESP32_DEVKIT1.IO26, IC7.In_5
  N5: MH-ET_LIVE_ESP32_DEVKIT1.IO27, IC7.In_4
  N6: MH-ET_LIVE_ESP32_DEVKIT1.IO14, IC7.In_3
  N7: MH-ET_LIVE_ESP32_DEVKIT1.IO12, IC7.In_2
  GND: MH-ET_LIVE_ESP32_DEVKIT1.GND, IC3.0V, IC4.0V, Part1.GND, M3.pin4, IC5.0V, IC6.0V, Part3.GND, IC7.0V
  N8: MH-ET_LIVE_ESP32_DEVKIT1.IO13, IC7.In_1
  N9: MH-ET_LIVE_ESP32_DEVKIT1.5V, MOTOR1.POS, MOTOR2.POS, MOTOR3.POS, MOTOR4.POS, MOTOR5.POS, MOTOR6.POS, MOTOR7.POS, MOTOR8.POS, MOTOR9.POS, MOTOR10.POS, MOTOR12.POS, MOTOR13.POS, MOTOR14.POS, MOTOR15.POS, MOTOR16.POS, IC3.COM_-_Common, IC4.COM_-_Common, MOTOR11.POS, Part1.V+, M3.pin3, IC5.COM_-_Common, IC6.COM_-_Common, Part3.V+, MOTOR17.POS, MOTOR18.POS, MOTOR19.POS, MOTOR20.POS, MOTOR21.POS, MOTOR22.POS, MOTOR23.POS, MOTOR24.POS, MOTOR25.POS, MOTOR26.POS, MOTOR27.POS, MOTOR28.POS, MOTOR29.POS, MOTOR30.POS, MOTOR31.POS, IC7.COM_-_Common, MOTOR32.POS, MOTOR33.POS, MOTOR34.POS, MOTOR35.POS, MOTOR36.POS, MOTOR37.POS, MOTOR38.POS, MOTOR39.POS, MOTOR40.POS
  N10: MH-ET_LIVE_ESP32_DEVKIT1.IO22, Part1.SCL, SparkFun_LiPo_Fuel_Gauge1.SCL, Part3.SCL
  N11: MH-ET_LIVE_ESP32_DEVKIT1.IO21, Part1.SDA, SparkFun_LiPo_Fuel_Gauge1.SDA, Part3.SDA
  N12: MOTOR1.NEG, IC3.Out_1
  N13: MOTOR2.NEG, IC3.Out_2
  N14: MOTOR3.NEG, IC3.Out_3
  N15: MOTOR4.NEG, IC3.Out_4
  N16: MOTOR5.NEG, IC3.Out_5
  N17: MOTOR6.NEG, IC3.Out_6
  N18: MOTOR7.NEG, IC3.Out_7
  N19: MOTOR8.NEG, IC3.Out_8
  N20: MOTOR9.NEG, IC4.Out_4
  N21: MOTOR10.NEG, IC4.Out_7
  N22: MOTOR12.NEG, IC4.Out_2
  N23: MOTOR13.NEG, IC4.Out_3
  N24: MOTOR14.NEG, IC4.Out_6
  N25: MOTOR15.NEG, IC4.Out_8
  N26: MOTOR16.NEG, IC4.Out_5
  N27: IC3.In_1, Part1.8
  N28: IC3.In_2, Part1.9
  N29: IC3.In_3, Part1.10
  N30: IC3.In_4, Part1.11
  N31: IC3.In_5, Part1.12
  N32: IC3.In_6, Part1.13
  N33: IC3.In_7, Part1.14
  N34: IC3.In_8, Part1.15
  N35: IC4.In_1, Part1.0
  N36: IC4.In_2, Part1.1
  N37: IC4.In_3, Part1.2
  N38: IC4.In_4, Part1.3
  N39: IC4.In_5, Part1.4
  N40: IC4.In_6, Part1.5
  N41: IC4.In_7, Part1.6
  N42: IC4.In_8, Part1.7
  N43: IC4.Out_1, MOTOR11.NEG
  N44: TP2.pin3, M3.pin2
  N45: TP2.pin4, SparkFun_LiPo_Fuel_Gauge1.VCC
  N46: TP2.pin5, SparkFun_LiPo_Fuel_Gauge1.GND
  N47: TP2.pin6, M3.pin1
  N48: IC5.In_1, Part3.0
  N49: IC5.In_2, Part3.1
  N50: IC5.In_3, Part3.2
  N51: IC5.In_4, Part3.3
  N52: IC5.In_5, Part3.4
  N53: IC5.In_6, Part3.5
  N54: IC5.In_7, Part3.6
  N55: IC5.In_8, Part3.7
  N56: IC5.Out_8, MOTOR20.NEG
  N57: IC5.Out_7, MOTOR19.NEG
  N58: IC5.Out_6, MOTOR23.NEG
  N59: IC5.Out_5, MOTOR22.NEG
  N60: IC5.Out_4, MOTOR21.NEG
  N61: IC5.Out_3, MOTOR17.NEG
  N62: IC5.Out_2, MOTOR24.NEG
  N63: IC5.Out_1, MOTOR18.NEG
  N64: IC6.In_1, Part3.8
  N65: IC6.In_2, Part3.9
  N66: IC6.In_3, Part3.10
  N67: IC6.In_4, Part3.11
  N68: IC6.In_5, Part3.12
  N69: IC6.In_6, Part3.13
  N70: IC6.In_7, Part3.14
  N71: IC6.In_8, Part3.15
  N72: IC6.Out_8, MOTOR40.NEG
  N73: IC6.Out_7, MOTOR30.NEG
  N74: IC6.Out_6, MOTOR29.NEG
  N75: IC6.Out_5, MOTOR31.NEG
  N76: IC6.Out_4, MOTOR25.NEG
  N77: IC6.Out_3, MOTOR26.NEG
  N78: IC6.Out_2, MOTOR28.NEG
  N79: IC6.Out_1, MOTOR27.NEG
  N80: IC7.Out_8, MOTOR36.NEG
  N81: IC7.Out_7, MOTOR38.NEG
  N82: IC7.Out_6, MOTOR37.NEG
  N83: IC7.Out_5, MOTOR39.NEG
  N84: IC7.Out_4, MOTOR32.NEG
  N85: IC7.Out_3, MOTOR33.NEG
  N86: IC7.Out_2, MOTOR35.NEG
  N87: IC7.Out_1, MOTOR34.NEG

notes:
  Option B: LiPo battery
  Option A: USB power bank

custom parts:
  MH-ET LIVE ESP32 DEVKIT 38 pins: http://mh.nodebb.com/topic/2/mh-et-live-esp32-devkit
  Vibration Motor: An eccentric vibration motor!
  16-Channel 12-bit PCA9685 PWM/Servo Driver: The Adafruit 16-Channel 12-bit PWM/Servo Driver will drive up to 16 servos over I2C with only 2 pins. The on-board PCA9685 PWM controller will drive all 16 channels simultaneously with no additional processing overhead. What's more, you can chain up to 62 of them to control up to 992 servos - all with the same 2 pins
  TP4056: A DIP stand-in part for whatever IC you want. With 6 pins on a 300mil dual inline package (DIP) footprint.
  Lithium Ion Polymer Battery 3.7v 1200mAh: Lithium ion polymer (also known as 'lipo' or 'lipoly') batteries are thin, light and powerful. The output ranges from 4.2V when completely charged to 3.7V. This battery has a capacity of 1200mAh for a total of about 4.5 Wh. The batteries come pre-attached with a genuine 2-pin JST-PH connector as shown and include the necessary protection circuitry.
  MT3608 Module: MT3608 Boost Converter Module Links: Aerosemi MT3608 2A Step Up Converter datasheet
  SparkFun LiPo Fuel Gauge: LiPo batteries are a great way to power your projects. They’re small, lightweight, and pack a pretty good punch for their size. Unfortunately, even the best batteries eventually run low on power and when they do it’s often unexpected (and at the worst time). Don’t be caught by surprise next time your board suddenly powers-down! The SparkFun LiPo Fuel Gauge connects your battery to your project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
