# Fritzing sketch schematic (saved by Fritzing 0.9.10b)
breadboards: 1

parts:
  MH-ET_LIVE_ESP32_DEVKIT1 = MH-ET LIVE ESP32 DEVKIT 38 pins
  MOTOR1 = Vibration Motor
  MOTOR2 = Vibration Motor
  MOTOR3 = Vibration Motor
  MOTOR4 = Vibration Motor
  MOTOR5 = Vibration Motor
  MOTOR6 = Vibration Motor
  MOTOR7 = Vibration Motor
  MOTOR8 = Vibration Motor
  MOTOR9 = Vibration Motor
  MOTOR10 = Vibration Motor
  MOTOR12 = Vibration Motor
  MOTOR13 = Vibration Motor
  MOTOR14 = Vibration Motor
  MOTOR15 = Vibration Motor
  MOTOR16 = Vibration Motor
  IC3 = ULN2803A [package=THT]
  IC4 = ULN2803A [package=THT]
  Part1 = Lithium Ion Polymer Battery 3.7v 1200mAh [part_number=258]
  M2 = MT3608 Module
  MOTOR11 = Vibration Motor
  TP1 = TP4056 [chip_label=TP4056 package="DIP (Dual Inline) [THT]"]

nets:
  N1: MH-ET_LIVE_ESP32_DEVKIT1.IO32, IC4.In_8
  N2: MH-ET_LIVE_ESP32_DEVKIT1.IO33, IC4.In_7
  N3: MH-ET_LIVE_ESP32_DEVKIT1.IO25, IC4.In_6
  N4: MH-ET_LIVE_ESP32_DEVKIT1.IO26, IC4.In_5
  N5: MH-ET_LIVE_ESP32_DEVKIT1.IO27, IC4.In_4
  N6: MH-ET_LIVE_ESP32_DEVKIT1.IO14, IC4.In_3
  N7: MH-ET_LIVE_ESP32_DEVKIT1.IO12, IC4.In_2
  N8: MH-ET_LIVE_ESP32_DEVKIT1.GND, IC3.0V, IC4.0V, M2.pin4
  N9: MH-ET_LIVE_ESP32_DEVKIT1.IO13, IC4.In_1
  N10: MH-ET_LIVE_ESP32_DEVKIT1.5V, MOTOR1.POS, MOTOR2.POS, MOTOR3.POS, MOTOR4.POS, MOTOR5.POS, MOTOR6.POS, MOTOR7.POS, MOTOR8.POS, MOTOR9.POS, MOTOR10.POS, MOTOR12.POS, MOTOR13.POS, MOTOR14.POS, MOTOR15.POS, MOTOR16.POS, IC3.COM_-_Common, IC4.COM_-_Common, M2.pin3, MOTOR11.POS
  N11: MH-ET_LIVE_ESP32_DEVKIT1.IO19, IC3.In_1
  N12: MH-ET_LIVE_ESP32_DEVKIT1.IO18, IC3.In_2
  N13: MH-ET_LIVE_ESP32_DEVKIT1.IO5, IC3.In_3
  N14: MH-ET_LIVE_ESP32_DEVKIT1.IO17, IC3.In_4
  N15: MH-ET_LIVE_ESP32_DEVKIT1.IO16, IC3.In_5
  N16: MH-ET_LIVE_ESP32_DEVKIT1.IO4, IC3.In_6
  N17: MH-ET_LIVE_ESP32_DEVKIT1.IO2, IC3.In_7
  N18: MH-ET_LIVE_ESP32_DEVKIT1.IO15, IC3.In_8
  N19: MOTOR1.NEG, IC3.Out_1
  N20: MOTOR2.NEG, IC3.Out_2
  N21: MOTOR3.NEG, IC3.Out_3
  N22: MOTOR4.NEG, IC3.Out_4
  N23: MOTOR5.NEG, IC3.Out_5
  N24: MOTOR6.NEG, IC3.Out_6
  N25: MOTOR7.NEG, IC3.Out_7
  N26: MOTOR8.NEG, IC3.Out_8
  N27: MOTOR9.NEG, IC4.Out_4
  N28: MOTOR10.NEG, IC4.Out_7
  N29: MOTOR12.NEG, IC4.Out_2
  N30: MOTOR13.NEG, IC4.Out_3
  N31: MOTOR14.NEG, IC4.Out_6
  N32: MOTOR15.NEG, IC4.Out_8
  N33: MOTOR16.NEG, IC4.Out_5
  N34: IC4.Out_1, MOTOR11.NEG
  N35: Part1.positive, TP1.pin4
  N36: Part1.negative, TP1.pin5
  N37: M2.pin1, TP1.pin6
  N38: M2.pin2, TP1.pin3

notes:
  0
  1
  2
  8
  9
  10
  Optional

custom parts:
  MH-ET LIVE ESP32 DEVKIT 38 pins: http://mh.nodebb.com/topic/2/mh-et-live-esp32-devkit
  Vibration Motor: An eccentric vibration motor!
  Lithium Ion Polymer Battery 3.7v 1200mAh: Lithium ion polymer (also known as 'lipo' or 'lipoly') batteries are thin, light and powerful. The output ranges from 4.2V when completely charged to 3.7V. This battery has a capacity of 1200mAh for a total of about 4.5 Wh. The batteries come pre-attached with a genuine 2-pin JST-PH connector as shown and include the necessary protection circuitry.
  MT3608 Module: MT3608 Boost Converter Module Links: Aerosemi MT3608 2A Step Up Converter datasheet
  TP4056: A DIP stand-in part for whatever IC you want. With 6 pins on a 300mil dual inline package (DIP) footprint.
